// Digital circuit 16SP.dig as structural Verilog
module _16SP (
  input  [15:0] x,
  input  [15:0] y,
  input  Cin,
  output [15:0] S,
  output Cout
);

  wire _4bitadder_d_1_cout, _4bitadder_d_2_cout, _4bitadder_d_3_cout;
  wire [3:0] _4bitadder_d_1_s, _4bitadder_d_2_s, _4bitadder_d_3_s, _4bitadder_d_4_s;

  // Probe c0 on Cin
  _4BitAdder_D _4bitadder_d_1 (
    .Cin(Cin), .Y(y[3:0]), .X(x[3:0]), .S(_4bitadder_d_1_s), .Cout(_4bitadder_d_1_cout));  // open: P, G
  // CorrectorD correctord_1: pin names not known; wires that end beside it: _4bitadder_d_1_s, _4bitadder_d_1_cout, S[3:0]
  // Probe c4 on _4bitadder_d_1_cout
  _4BitAdder_D _4bitadder_d_2 (
    .Cin(_4bitadder_d_1_cout), .Y(y[7:4]), .X(x[7:4]), .S(_4bitadder_d_2_s), .Cout(_4bitadder_d_2_cout));  // open: P, G
  // Probe s3 on S[3:0]
  // CorrectorD correctord_2: pin names not known; wires that end beside it: _4bitadder_d_2_s, _4bitadder_d_2_cout, S[7:4]
  // Probe c8 on _4bitadder_d_2_cout
  _4BitAdder_D _4bitadder_d_3 (
    .Cin(_4bitadder_d_2_cout), .Y(y[11:8]), .X(x[11:8]), .S(_4bitadder_d_3_s), .Cout(_4bitadder_d_3_cout));  // open: P, G
  // Probe s7 on S[7:4]
  // CorrectorD correctord_3: pin names not known; wires that end beside it: _4bitadder_d_3_s, _4bitadder_d_3_cout, S[11:8]
  // Probe c12 on _4bitadder_d_3_cout
  _4BitAdder_D _4bitadder_d_4 (
    .Cin(_4bitadder_d_3_cout), .Y(y[15:12]), .X(x[15:12]), .S(_4bitadder_d_4_s), .Cout(Cout));  // open: P, G
  // Probe s11 on S[11:8]
  // CorrectorD correctord_4: pin names not known; wires that end beside it: _4bitadder_d_4_s, Cout, S[15:12]
  // Probe c16 on Cout
  // Probe s15 on S[15:12]

  // Notes on the sheet:
  //   x: default 34952
  //   y: default 30583
endmodule
