// Digital circuit 2421SingleLevelCLA_D.dig as structural Verilog
module _2421SingleLevelCLA_D (
  input  [15:0] X,
  input  [15:0] Y,
  input  Cin,
  output [15:0] S,
  output Cout
);

  wire _4bitadder_d_1_cout, _4bitadder_d_2_cout, _4bitadder_d_3_cout;
  wire [3:0] _4bitadder_d_1_s, _4bitadder_d_2_s, _4bitadder_d_3_s, _4bitadder_d_4_s;

  _4BitAdder_D _4bitadder_d_1 (
    .Cin(Cin), .Y(Y[3:0]), .X(X[3:0]), .S(_4bitadder_d_1_s), .Cout(_4bitadder_d_1_cout));  // open: P, G
  // CorrectorD correctord_1: pin names not known; wires that end beside it: _4bitadder_d_1_s, _4bitadder_d_1_cout, S[3:0]
  _4BitAdder_D _4bitadder_d_2 (
    .Cin(_4bitadder_d_1_cout), .Y(Y[7:4]), .X(X[7:4]), .S(_4bitadder_d_2_s), .Cout(_4bitadder_d_2_cout));  // open: P, G
  // CorrectorD correctord_2: pin names not known; wires that end beside it: _4bitadder_d_2_s, _4bitadder_d_2_cout, S[7:4]
  _4BitAdder_D _4bitadder_d_3 (
    .Cin(_4bitadder_d_2_cout), .Y(Y[11:8]), .X(X[11:8]), .S(_4bitadder_d_3_s), .Cout(_4bitadder_d_3_cout));  // open: P, G
  // CorrectorD correctord_3: pin names not known; wires that end beside it: _4bitadder_d_3_s, _4bitadder_d_3_cout, S[11:8]
  _4BitAdder_D _4bitadder_d_4 (
    .Cin(_4bitadder_d_3_cout), .Y(Y[15:12]), .X(X[15:12]), .S(_4bitadder_d_4_s), .Cout(Cout));  // open: P, G
  // CorrectorD correctord_4: pin names not known; wires that end beside it: _4bitadder_d_4_s, Cout, S[15:12]
endmodule
