// Digital circuit 2421TwoLevelCLA.dig as structural Verilog
module _2421TwoLevelCLA (
  input  [15:0] X,
  input  [15:0] Y,
  input  Cin,
  output Cout,
  output [15:0] S
);

  wire extendedcla_1_c4, extendedcla_1_c8, extendedcla_1_c12;
  wire [3:0] _4bitadder_1_s, _4bitadder_2_s, _4bitadder_3_s, _4bitadder_4_s, g, p;

  _4BitAdder _4bitadder_1 (.Cin(Cin), .Y(Y[3:0]), .X(X[3:0]), .S(_4bitadder_1_s), .G(g[0]), .P(p[0]));  // open: Cout
  ExtendedCLA extendedcla_1 (
    .Cin(Cin), .p(p), .g(g), .c4(extendedcla_1_c4), .c8(extendedcla_1_c8), .c12(extendedcla_1_c12), .c16(Cout));  // open: S, G_2, P_2
  // Corrector corrector_1: pin names not known; wires that end beside it: _4bitadder_1_s, extendedcla_1_c4, S[3:0]
  _4BitAdder _4bitadder_2 (
    .Cin(extendedcla_1_c4), .Y(Y[7:4]), .X(X[7:4]), .S(_4bitadder_2_s), .G(g[1]), .P(p[1]));  // open: Cout
  // Corrector corrector_2: pin names not known; wires that end beside it: _4bitadder_2_s, extendedcla_1_c8, S[7:4]
  _4BitAdder _4bitadder_3 (
    .Cin(extendedcla_1_c8), .Y(Y[11:8]), .X(X[11:8]), .S(_4bitadder_3_s), .G(g[2]), .P(p[2]));  // open: Cout
  // Corrector corrector_3: pin names not known; wires that end beside it: _4bitadder_3_s, extendedcla_1_c12, S[11:8]
  _4BitAdder _4bitadder_4 (
    .Cin(extendedcla_1_c12), .Y(Y[15:12]), .X(X[15:12]), .S(_4bitadder_4_s), .G(g[3]), .P(p[3]));  // open: Cout
  // Corrector corrector_4: pin names not known; wires that end beside it: _4bitadder_4_s, Cout, S[15:12]

  // Other names for the same wires on the sheet: c0 = Cin
endmodule
