// Digital circuit 2421TwoLevelCLA_D.dig as structural Verilog
module _2421TwoLevelCLA_D (
  input  [15:0] X,
  input  [15:0] Y,
  input  Cin,
  output Cout,
  output [15:0] S
);

  wire extendedcla_d_1_c4, extendedcla_d_1_c8, extendedcla_d_1_c12;
  wire [3:0] _4bitadder_d_1_s, _4bitadder_d_2_s, _4bitadder_d_3_s, _4bitadder_d_4_s, g, p;

  _4BitAdder_D _4bitadder_d_1 (
    .Cin(Cin), .Y(Y[3:0]), .X(X[3:0]), .S(_4bitadder_d_1_s), .P(p[0]), .G(g[0]));  // open: Cout
  ExtendedCLA_D extendedcla_d_1 (
    .Cin(Cin), .p(p), .g(g), .c4(extendedcla_d_1_c4), .c8(extendedcla_d_1_c8), .c12(extendedcla_d_1_c12),
    .c16(Cout));  // open: S, P_2, G_2
  // CorrectorD correctord_1: pin names not known; wires that end beside it: _4bitadder_d_1_s, extendedcla_d_1_c4, S[3:0]
  _4BitAdder_D _4bitadder_d_2 (
    .Cin(extendedcla_d_1_c4), .Y(Y[7:4]), .X(X[7:4]), .S(_4bitadder_d_2_s), .P(p[1]), .G(g[1]));  // open: Cout
  // CorrectorD correctord_2: pin names not known; wires that end beside it: _4bitadder_d_2_s, extendedcla_d_1_c8, S[7:4]
  _4BitAdder_D _4bitadder_d_3 (
    .Cin(extendedcla_d_1_c8), .Y(Y[11:8]), .X(X[11:8]), .S(_4bitadder_d_3_s), .P(p[2]), .G(g[2]));  // open: Cout
  // CorrectorD correctord_3: pin names not known; wires that end beside it: _4bitadder_d_3_s, extendedcla_d_1_c12, S[11:8]
  _4BitAdder_D _4bitadder_d_4 (
    .Cin(extendedcla_d_1_c12), .Y(Y[15:12]), .X(X[15:12]), .S(_4bitadder_d_4_s), .P(p[3]), .G(g[3]));  // open: Cout
  // CorrectorD correctord_4: pin names not known; wires that end beside it: _4bitadder_d_4_s, Cout, S[15:12]

  // Other names for the same wires on the sheet: c0 = Cin
endmodule
