// Digital circuit 4BitAdder.dig as structural Verilog
module _4BitAdder (
  input  Cin,
  input  [3:0] Y,
  input  [3:0] X,
  output [3:0] S,
  output Cout,
  output G,
  output P
);

  wire and_2_out, and_4_out, and_6_out, and_9_out, and_10_out, c1, c2, c3, g0, g1, g2, g3, or_1_out,
       or_2_out, or_3_out, or_4_out, or_5_out, or_6_out, or_7_out, or_11_out, or_13_out, or_15_out, p0, p1,
       p2, p3;

  or or_1 (or_1_out, P, Cin);
  and and_1 (Cout, or_1_out, G);
  xnor xnor_1 (S[3], p3, c3);
  xnor xnor_2 (S[2], p2, c2);
  or or_2 (or_2_out, Cin, p0, p1, p2);
  xnor xnor_3 (S[1], p1, c1);
  or or_3 (or_3_out, g0, p1, p2);
  xnor xnor_4 (S[0], p0, Cin);
  or or_4 (or_4_out, g1, p2);
  and and_2 (and_2_out, and_4_out, or_3_out);
  and and_3 (c3, and_2_out, or_2_out);
  and and_4 (and_4_out, g2, or_4_out);
  xnor xnor_5 (p3, X[3], Y[3]);
  or or_5 (or_5_out, Cin, p0, p1);
  xnor xnor_6 (p2, X[2], Y[2]);
  or or_6 (or_6_out, g0, p1);
  and and_5 (c2, and_6_out, or_5_out);
  xnor xnor_7 (p1, X[1], Y[1]);
  and and_6 (and_6_out, g1, or_6_out);
  xnor xnor_8 (p0, X[0], Y[0]);
  or or_7 (or_7_out, Cin, p0);
  and and_7 (c1, g0, or_7_out);
  or or_8 (P, p0, p1, p2, p3);
  or or_9 (g3, Y[3], X[3]);
  or or_10 (g2, Y[2], X[2]);
  or or_11 (or_11_out, g0, p1, p2, p3);
  or or_12 (g1, Y[1], X[1]);
  or or_13 (or_13_out, g1, p2, p3);
  and and_8 (G, and_10_out, or_11_out);
  or or_14 (g0, Y[0], X[0]);
  or or_15 (or_15_out, g2, p3);
  and and_9 (and_9_out, g3, or_15_out);
  and and_10 (and_10_out, and_9_out, or_13_out);

  // Other names for the same wires on the sheet: c0 = Cin; c4 = Cout

  // Notes on the sheet:
  //   Look-Ahead
  //   Summation
  //   PG Generator
  //   P and G
endmodule
