// Digital circuit 4BitAdder_DP.dig as structural Verilog
module _4BitAdder_DP (
  input  Cin,
  input  [3:0] Y,
  input  [3:0] X,
  output [3:0] S,
  output Cout,
  output P,
  output G
);

  wire andd_2_p2, andd_3_p2, andd_5_p2, andd_8_p2, andd_9_p3, c1, c2, c3, g0, g1, g2, g3, ord_1_p2, ord_2_p3,
       ord_3_p3, ord_4_p2, ord_5_p3, ord_6_p2, ord_7_p2, ord_11_p2, ord_13_p3, ord_15_p2, p0, p1, p2, p3;

  // OrD #(.generic("inputCount := 2;")) ord_1: pin names not known; wires that end beside it: Cin, ord_1_p2, P
  // AndD #(.generic("inputCount := 2;")) andd_1: pin names not known; wires that end beside it: ord_1_p2, G
  // XnorD #(.generic("inputCount := 2;")) xnord_1: pin names not known; wires that end beside it: c3, S[3], p3
  // Probe c4 on Cout
  // XnorD #(.generic("inputCount := 2;")) xnord_2: pin names not known; wires that end beside it: c2, S[2], p2
  // OrD #(.generic("inputCount := 4;")) ord_2: pin names not known; wires that end beside it: p2, p1, ord_2_p3, p0, Cin
  // XnorD #(.generic("inputCount := 2;")) xnord_3: pin names not known; wires that end beside it: c1, S[1], p1
  // OrD #(.generic("inputCount := 3;")) ord_3: pin names not known; wires that end beside it: p2, p1, ord_3_p3, g0
  // XnorD #(.generic("inputCount := 2;")) xnord_4: pin names not known; wires that end beside it: Cin, S[0], p0
  // OrD #(.generic("inputCount := 2;")) ord_4: pin names not known; wires that end beside it: p2, ord_4_p2, g1
  // AndD #(.generic("inputCount := 2;")) andd_2: pin names not known; wires that end beside it: ord_3_p3, andd_2_p2, andd_2_p2
  // AndD #(.generic("inputCount := 2;")) andd_3: pin names not known; wires that end beside it: ord_2_p3, andd_3_p2, andd_3_p2
  // Probe c3 on c3
  // AndD #(.generic("inputCount := 2;")) andd_4: pin names not known; wires that end beside it: ord_4_p2, g2
  // XnorD #(.generic("inputCount := 2;")) xnord_5: pin names not known; wires that end beside it: Y[3], p3, X[3]
  // OrD #(.generic("inputCount := 3;")) ord_5: pin names not known; wires that end beside it: p1, p0, ord_5_p3, Cin
  // XnorD #(.generic("inputCount := 2;")) xnord_6: pin names not known; wires that end beside it: Y[2], p2, X[2]
  // OrD #(.generic("inputCount := 2;")) ord_6: pin names not known; wires that end beside it: p1, ord_6_p2, g0
  // AndD #(.generic("inputCount := 2;")) andd_5: pin names not known; wires that end beside it: ord_5_p3, andd_5_p2, andd_5_p2
  // XnorD #(.generic("inputCount := 2;")) xnord_7: pin names not known; wires that end beside it: Y[1], p1, X[1], Y[0]
  // AndD #(.generic("inputCount := 2;")) andd_6: pin names not known; wires that end beside it: ord_6_p2, g1
  // Probe c2 on c2
  // XnorD #(.generic("inputCount := 2;")) xnord_8: pin names not known; wires that end beside it: p0, X[0]
  // OrD #(.generic("inputCount := 2;")) ord_7: pin names not known; wires that end beside it: p0, ord_7_p2, Cin
  // AndD #(.generic("inputCount := 2;")) andd_7: pin names not known; wires that end beside it: ord_7_p2, g0
  // Probe c1 on c1
  // Probe c0 on Cin
  // OrD #(.generic("inputCount := 4;")) ord_8: pin names not known; wires that end beside it: p3, p2, P, p1, p0, p3
  // OrD #(.generic("inputCount := 2;")) ord_9: pin names not known; wires that end beside it: X[3], g3, Y[3], X[2]
  // OrD #(.generic("inputCount := 2;")) ord_10: pin names not known; wires that end beside it: g2, Y[2], X[1]
  // OrD #(.generic("inputCount := 4;")) ord_11: pin names not known; wires that end beside it: p2, ord_11_p2, p1, g0
  // OrD #(.generic("inputCount := 2;")) ord_12: pin names not known; wires that end beside it: g1, Y[1], X[0]
  // OrD #(.generic("inputCount := 3;")) ord_13: pin names not known; wires that end beside it: p3, p2, ord_13_p3, g1
  // OrD #(.generic("inputCount := 2;")) ord_14: pin names not known; wires that end beside it: g0, Y[0]
  // OrD #(.generic("inputCount := 2;")) ord_15: pin names not known; wires that end beside it: p3, ord_15_p2, g2
  // AndD #(.generic("inputCount := 2;")) andd_8: pin names not known; wires that end beside it: ord_13_p3, andd_8_p2, andd_8_p2
  // AndD #(.generic("inputCount := 2;")) andd_9: pin names not known; wires that end beside it: ord_11_p2, G, andd_9_p3, andd_9_p3
  // AndD #(.generic("inputCount := 2;")) andd_10: pin names not known; wires that end beside it: ord_15_p2, g3

  // Other names for the same wires on the sheet: c0 = Cin; c4 = Cout

  // Notes on the sheet:
  //   Y: default 7
  //   X: default 8
  //   Look-Ahead
  //   Summation
  //   PG Generator
  //   P and G
endmodule
