// Digital circuit ExtendedCLA.dig as structural Verilog
module ExtendedCLA (
  input  Cin,
  input  [3:0] p,
  input  [3:0] g,
  output [3:0] S,
  output G_2,
  output P_2,
  output c4,
  output c8,
  output c12,
  output c16
);

  wire and_2_out, and_4_out, and_6_out, and_8_out, and_10_out, or_1_out, or_2_out, or_3_out, or_4_out,
       or_5_out, or_6_out, or_7_out, or_9_out, or_10_out, or_11_out;

  and and_1 (c16, or_1_out, G_2);
  xnor xnor_1 (S[3], p[3], c12);
  or or_1 (or_1_out, P_2, Cin);
  xnor xnor_2 (S[2], p[2], c8);
  or or_2 (or_2_out, Cin, p[0], p[1], p[2]);
  xnor xnor_3 (S[1], p[1], c4);
  or or_3 (or_3_out, g[0], p[1], p[2]);
  xnor xnor_4 (S[0], p[0], Cin);
  or or_4 (or_4_out, g[1], p[2]);
  and and_2 (and_2_out, and_4_out, or_3_out);
  and and_3 (c12, and_2_out, or_2_out);
  and and_4 (and_4_out, g[2], or_4_out);
  or or_5 (or_5_out, Cin, p[0], p[1]);
  or or_6 (or_6_out, g[0], p[1]);
  and and_5 (c8, and_6_out, or_5_out);
  and and_6 (and_6_out, g[1], or_6_out);
  or or_7 (or_7_out, Cin, p[0]);
  and and_7 (c4, g[0], or_7_out);
  or or_8 (P_2, p[0], p[1], p[2], p[3]);
  or or_9 (or_9_out, g[0], p[1], p[2], p[3]);
  or or_10 (or_10_out, g[1], p[2], p[3]);
  or or_11 (or_11_out, g[2], p[3]);
  and and_8 (and_8_out, and_10_out, or_10_out);
  and and_9 (G_2, and_8_out, or_9_out);
  and and_10 (and_10_out, g[3], or_11_out);

  // Other names for the same wires on the sheet: c0 = Cin; c1 = c4; c2 = c8; c3 = c12; c4_t = c16; G_t = G_2;
  //   P_t = P_2

  // Notes on the sheet:
  //   Look-Ahead
  //   Summation
  //   P and G
endmodule
