// Digital circuit ExtendedCLA_D.dig as structural Verilog
module ExtendedCLA_D (
  input  Cin,
  input  [3:0] p,
  input  [3:0] g,
  output [3:0] S,
  output c4,
  output c8,
  output c12,
  output c16,
  output P_2,
  output G_2
);

  wire andd_2_p2, andd_3_p3, andd_6_p3, andd_8_p2, andd_9_p3, ord_1_p2, ord_2_p3, ord_3_p3, ord_4_p2,
       ord_5_p3, ord_6_p2, ord_7_p2, ord_9_p2, ord_10_p3, ord_11_p2;

  // OrD #(.generic("inputCount := 2;")) ord_1: pin names not known; wires that end beside it: Cin, ord_1_p2, P_2
  // XnorD #(.generic("inputCount := 2;")) xnord_1: pin names not known; wires that end beside it: c12, S[3], p[3]
  // AndD #(.generic("inputCount := 2;")) andd_1: pin names not known; wires that end beside it: ord_1_p2, c16, G_2
  // XnorD #(.generic("inputCount := 2;")) xnord_2: pin names not known; wires that end beside it: c8, S[2], p[2]
  // OrD #(.generic("inputCount := 4;")) ord_2: pin names not known; wires that end beside it: p[2], p[1], ord_2_p3, p[0], Cin
  // XnorD #(.generic("inputCount := 2;")) xnord_3: pin names not known; wires that end beside it: c4, S[1], p[1]
  // OrD #(.generic("inputCount := 3;")) ord_3: pin names not known; wires that end beside it: p[2], p[1], ord_3_p3, g[0]
  // XnorD #(.generic("inputCount := 2;")) xnord_4: pin names not known; wires that end beside it: Cin, S[0], p[0]
  // OrD #(.generic("inputCount := 2;")) ord_4: pin names not known; wires that end beside it: p[2], ord_4_p2, g[1]
  // AndD #(.generic("inputCount := 2;")) andd_2: pin names not known; wires that end beside it: ord_3_p3, andd_2_p2, andd_2_p2
  // AndD #(.generic("inputCount := 2;")) andd_3: pin names not known; wires that end beside it: ord_2_p3, c12, andd_3_p3, andd_3_p3
  // AndD #(.generic("inputCount := 2;")) andd_4: pin names not known; wires that end beside it: ord_4_p2, g[2]
  // OrD #(.generic("inputCount := 3;")) ord_5: pin names not known; wires that end beside it: p[1], p[0], ord_5_p3, Cin
  // OrD #(.generic("inputCount := 2;")) ord_6: pin names not known; wires that end beside it: p[1], ord_6_p2, g[0]
  // AndD #(.generic("inputCount := 2;")) andd_5: pin names not known; wires that end beside it: ord_6_p2, g[1]
  // AndD #(.generic("inputCount := 2;")) andd_6: pin names not known; wires that end beside it: ord_5_p3, c8, andd_6_p3, andd_6_p3
  // OrD #(.generic("inputCount := 2;")) ord_7: pin names not known; wires that end beside it: p[0], ord_7_p2, Cin
  // AndD #(.generic("inputCount := 2;")) andd_7: pin names not known; wires that end beside it: ord_7_p2, c4, g[0]
  // OrD #(.generic("inputCount := 4;")) ord_8: pin names not known; wires that end beside it: p[3], p[2], P_2, p[1], p[0], p[3]
  // OrD #(.generic("inputCount := 4;")) ord_9: pin names not known; wires that end beside it: p[2], ord_9_p2, p[1], g[0]
  // OrD #(.generic("inputCount := 3;")) ord_10: pin names not known; wires that end beside it: p[3], p[2], ord_10_p3, g[1]
  // OrD #(.generic("inputCount := 2;")) ord_11: pin names not known; wires that end beside it: p[3], ord_11_p2, g[2]
  // AndD #(.generic("inputCount := 2;")) andd_8: pin names not known; wires that end beside it: ord_10_p3, andd_8_p2, andd_8_p2
  // AndD #(.generic("inputCount := 2;")) andd_9: pin names not known; wires that end beside it: ord_9_p2, G_2, andd_9_p3, andd_9_p3
  // AndD #(.generic("inputCount := 2;")) andd_10: pin names not known; wires that end beside it: ord_11_p2, g[3]

  // Other names for the same wires on the sheet: c0 = Cin; c1 = c4; c2 = c8; c3 = c12; c4_t = c16; G_t = G_2;
  //   P_t = P_2

  // Notes on the sheet:
  //   Look-Ahead
  //   Summation
  //   P and G
endmodule
