// Digital circuit HazardFree.dig as structural Verilog
module HazardFree (
  input  A,
  input  B,
  input  C,
  input  D,
  output C1,
  output C2
);

  wire A_t, andd_1_p3, andd_2_p3, andd_3_p3, andd_4_p3, B_t, C_t, D_t, ord_1_p4, ord_2_p4, ord_3_p4,
       ord_4_p4, ord_5_p4;

  not not_1 (A_t, A);
  not not_2 (B_t, B);
  not not_3 (C_t, C);
  not not_4 (D_t, D);
  // AndD #(.generic("inputCount := 2;")) andd_1: pin names not known; wires that end beside it: A_t, D_t, andd_1_p3
  // AndD #(.generic("inputCount := 2;")) andd_2: pin names not known; wires that end beside it: A, D, andd_2_p3
  // AndD #(.generic("inputCount := 2;")) andd_3: pin names not known; wires that end beside it: C, D, andd_3_p3
  // AndD #(.generic("inputCount := 2;")) andd_4: pin names not known; wires that end beside it: C_t, D_t, andd_4_p3
  // OrD #(.generic("inputCount := 3;")) ord_1: pin names not known; wires that end beside it: A, B_t, C_t, ord_1_p4
  // OrD #(.generic("inputCount := 3;")) ord_2: pin names not known; wires that end beside it: A_t, B, C, ord_2_p4
  // OrD #(.generic("inputCount := 3;")) ord_3: pin names not known; wires that end beside it: A, B, D_t, ord_3_p4
  // OrD #(.generic("inputCount := 3;")) ord_4: pin names not known; wires that end beside it: A_t, B_t, D, ord_4_p4
  // OrD #(.generic("inputCount := 3;")) ord_5: pin names not known; wires that end beside it: A_t, C, D, ord_5_p4
  or or_1 (C1, andd_1_p3, andd_2_p3, andd_3_p3, andd_4_p3);
  and and_1 (C2, ord_1_p4, ord_2_p4, ord_3_p4, ord_4_p4, ord_5_p4);
endmodule
