// Digital circuit SingleLevelCLA.dig as structural Verilog
module SingleLevelCLA (
  input  [15:0] X,
  input  [15:0] Y,
  input  Cin,
  output [15:0] S,
  output Cout
);

  wire _4bitadder_1_cout, _4bitadder_2_cout, _4bitadder_3_cout;

  _4BitAdder _4bitadder_1 (.Cin(Cin), .Y(Y[3:0]), .X(X[3:0]), .S(S[3:0]), .Cout(_4bitadder_1_cout));  // open: G, P
  _4BitAdder _4bitadder_2 (
    .Cin(_4bitadder_1_cout), .Y(Y[7:4]), .X(X[7:4]), .S(S[7:4]), .Cout(_4bitadder_2_cout));  // open: G, P
  _4BitAdder _4bitadder_3 (
    .Cin(_4bitadder_2_cout), .Y(Y[11:8]), .X(X[11:8]), .S(S[11:8]), .Cout(_4bitadder_3_cout));  // open: G, P
  _4BitAdder _4bitadder_4 (
    .Cin(_4bitadder_3_cout), .Y(Y[15:12]), .X(X[15:12]), .S(S[15:12]), .Cout(Cout));  // open: G, P
endmodule
