// Digital circuit TwoLevelCLA.dig as structural Verilog
module TwoLevelCLA (
  input  [15:0] X,
  input  [15:0] Y,
  input  Cin,
  output [15:0] S,
  output Cout
);

  wire extendedcla_1_c4, extendedcla_1_c8, extendedcla_1_c12;
  wire [3:0] g, p;

  _4BitAdder _4bitadder_1 (.Cin(Cin), .Y(Y[3:0]), .X(X[3:0]), .S(S[3:0]), .G(g[0]), .P(p[0]));  // open: Cout
  ExtendedCLA extendedcla_1 (
    .Cin(Cin), .p(p), .g(g), .c4(extendedcla_1_c4), .c8(extendedcla_1_c8), .c12(extendedcla_1_c12), .c16(Cout));  // open: S, G_2, P_2
  _4BitAdder _4bitadder_2 (
    .Cin(extendedcla_1_c4), .Y(Y[7:4]), .X(X[7:4]), .S(S[7:4]), .G(g[1]), .P(p[1]));  // open: Cout
  _4BitAdder _4bitadder_3 (
    .Cin(extendedcla_1_c8), .Y(Y[11:8]), .X(X[11:8]), .S(S[11:8]), .G(g[2]), .P(p[2]));  // open: Cout
  _4BitAdder _4bitadder_4 (
    .Cin(extendedcla_1_c12), .Y(Y[15:12]), .X(X[15:12]), .S(S[15:12]), .G(g[3]), .P(p[3]));  // open: Cout

  // Other names for the same wires on the sheet: c0 = Cin
endmodule
